# Fritzing sketch RZ67 Seeed XIAO ESP32C3 (saved by Fritzing 0.9.10b)
breadboards: 1

parts:
  Mod1 = seeeduino-xiao
  Q1 = Basic FET N-Channel [package="DPak [SMD]"]
  J1 = female pin header, 3 pins [form="♀ (female)"]

nets:
  N1: Mod1.D6, Q1.Gate
  N2: Mod1.GND, Q1.source, J1.pin2, J1.pin3
  N3: Q1.drain, J1.pin1

notes:
  Seeed Studio XIAO ESP32C3 has a battery connection on the bottom side. In my implementation I have soldered the battery connection to a LIPO battery before soldering the XIAO to the breadboard.
  Header is to illustrate cable to Mamiya RZ67.
  Mamiya's pinout is, from left to right:
  - 6V PWR
  - GRD
  - S1
  - S2
  To trigger the shutter release from the ESP32, we need to connect GND, S1 and S2 via the MOSFET. PWR can be ignored.

custom parts:
  seeeduino-xiao: Seeeduino XIAO processor board.
